# Fritzing sketch esphome termostato emmeti (saved by Fritzing 0.9.3b)

parts:
  TTL_-->_RS485 = RS485_XY-017 [part_number=XY-017]
  D1_MINI = WeMos D1 Mini
  DC-DC_STEP_DOWN = mini560 [part_number=Mini560 package=THT]
  THERMOSTAT = Termostato BUS - Pannello Comando [package="Pannello a parete"]

nets:
  N1: TTL_-->_RS485.GND, D1_MINI.G, DC-DC_STEP_DOWN.pin_3, DC-DC_STEP_DOWN.pin_6, DC-DC_STEP_DOWN.pin_7, THERMOSTAT.-
  N2: TTL_-->_RS485.A, THERMOSTAT.A
  N3: TTL_-->_RS485.B, THERMOSTAT.B
  VCC: TTL_-->_RS485.VCC, D1_MINI.5V, DC-DC_STEP_DOWN.pin_8, DC-DC_STEP_DOWN.pin_9
  N4: TTL_-->_RS485.TXD, D1_MINI.RX
  N5: TTL_-->_RS485.RXD, D1_MINI.TX
  N6: DC-DC_STEP_DOWN.pin_1, DC-DC_STEP_DOWN.pin_2, THERMOSTAT.+

custom parts:
  RS485_XY-017: Commercially available RS485 to RS232 TTL Module
  mini560: 5A DC-DC Mini 560 Step Down Stabilized Voltage Supply Module Output 3.3 5V 9V 12V Step-down Power Converter Board Module
  Termostato BUS - Pannello Comando: Pannello di comando/termostato con display e collegamento a BUS 2 fili (morsetti +, A, B, -) e contatto consenso, con morsetti di loop (A, A, B, B, -) per il collegamento a catena verso un'altra unità. Componente ricostruito dall'immagine del frontalino e della morsettiera fornite dall'utente: verificare i riferimenti dei morsetti sul manuale del dispositivo reale prima del cablaggio.
